# Fritzing sketch mqtt-esp8266-wiring (saved by Fritzing 0.9.3b)
breadboards: 1

parts:
  S2 = Round Pushbutton
  LED1 = LED - 5mm [color="Red (633nm)" package="5 mm [THT]"]
  LED2 = LED - 5mm [color="Green (555nm)" package="5 mm [THT]"]
  S3 = Round Pushbutton
  WeMos_D1_Mini1 = WeMos D1 Mini
  WeMos_D1_Mini2 = WeMos D1 Mini

nets:
  N1: S2.leg0, LED1.cathode, LED2.cathode, S3.leg1, WeMos_D1_Mini1.G, WeMos_D1_Mini2.G
  N2: S2.leg1, WeMos_D1_Mini1.D2
  N3: LED1.anode, WeMos_D1_Mini2.D1
  N4: LED2.anode, WeMos_D1_Mini1.D1
  N5: S3.leg0, WeMos_D1_Mini2.D2
